# Fritzing sketch RasPi-Mogura (saved by Fritzing 0.9.2b)
circuit board: 8.46667cm x 5.64444cm
breadboards: 1

parts:
  Raspberry_Pi1 = Raspberry Pi 2
  S1 = Pushbutton [package="[THT]"]
  S2 = Pushbutton [package="[THT]"]
  S3 = Pushbutton [package="[THT]"]
  S4 = Pushbutton [package="[THT]"]
  LED1 = LED - 5mm [color="Red (633nm)" package="5 mm [THT]"]
  LED2 = LED - 5mm [color="Red (633nm)" package="5 mm [THT]"]
  LED3 = LED - 5mm [color="Red (633nm)" package="5 mm [THT]"]
  LED4 = LED - 5mm [color="Red (633nm)" package="5 mm [THT]"]
  SPKR1 = Loudspeaker
  R1 = Resistor [tolerance=±10% resistance=220 package="2010 [SMD]"]

nets:
  N1: Raspberry_Pi1.GPIO10, LED1.anode
  N2: Raspberry_Pi1.GPIO9, LED2.anode
  N3: Raspberry_Pi1.GPIO11, LED3.anode
  N4: Raspberry_Pi1.ID_SD, LED4.anode
  N5: Raspberry_Pi1.GPIO6, S1.Pin_1, S1.Pin_2
  N6: Raspberry_Pi1.GPIO13, S2.Pin_1, S2.Pin_2
  N7: Raspberry_Pi1.GPIO19, S3.Pin_1, S3.Pin_2
  N8: Raspberry_Pi1.GPIO26, S4.Pin_1, S4.Pin_2
  N9: Raspberry_Pi1.GND, S1.Pin_3, S1.Pin_4, S2.Pin_3, S2.Pin_4, S3.Pin_3, S3.Pin_4, S4.Pin_3, S4.Pin_4, LED1.cathode, LED2.cathode, LED3.cathode, LED4.cathode, SPKR1.pin2, R1.Pin_1
  N10: Raspberry_Pi1.GPIO21, SPKR1.pin1, R1.Pin_0
